# Fritzing sketch blueprint (saved by Fritzing 0.9.1b)
breadboards: 3

parts:
  Part1 = Intel Edison Arduinobreakout
  Part2 = SRF05 Ultrasonic Rangefinder
  Part3 = SRF05 Ultrasonic Rangefinder
  J1 = Basic Servo

nets:
  N1: Part1.D8, Part2.Trig
  N2: Part1.D9_PWM, J1.pulse
  N3: Part1.D12/MISO, Part3.Echo
  N4: Part1.D13/SCK, Part3.Trig
  N5: Part1.D7, Part2.Echo
  VCC: Part1.5V, Part2.VCC, Part3.VCC, J1.vcc
  GND: Part1.GND, Part2.GND, Part3.GND, J1.gnd
